// Logisim project sqrt2.circ as structural Verilog: 22 circuits, main circuit main
module main (
  input  ENABLE,
  input  [15:0] IO_DATA_IN,
  output NAN,
  output PINF,
  output NINF,
  output RESULT,
  output [15:0] IO_DATA_OUT
);

  wire CLK_out;

  Clock CLK (.out(CLK_out));
  sqrt sqrt_1 (
    .CLK(CLK_out), .ENABLE(ENABLE), .IO_DATA_IN(IO_DATA_IN), .IS_NAN(NAN), .IS_PINF(PINF), .IS_NINF(NINF),
    .RESULT(RESULT), .IO_DATA_OUT(IO_DATA_OUT));
endmodule

module sqrt (
  input  CLK,
  input  ENABLE,
  input  [15:0] IO_DATA_IN,
  output IS_NAN,
  output IS_PINF,
  output IS_NINF,
  output RESULT,
  output [15:0] IO_DATA_OUT
);

  wire get_info_1_sign;
  wire [4:0] get_info_1_exp;
  wire [9:0] get_info_1_mantissa;

  get_info get_info_1 (
    .IO_IN(IO_DATA_IN), .mantissa(get_info_1_mantissa), .exp(get_info_1_exp), .sign(get_info_1_sign));
  special_cases special_cases_1 (
    .mant(get_info_1_mantissa), .exp(get_info_1_exp), .sign(get_info_1_sign), .NAN(IS_NAN), .PINF(IS_PINF),
    .NINF(IS_NINF));

  assign IO_DATA_OUT = IO_DATA_IN;
endmodule

module shift_left (
  input  [15:0] IO_IN,
  output [15:0] IO_OUT
);

  // NoConnect on IO_IN[15]

  assign IO_OUT = {IO_IN[14:0], 1'b0};
endmodule

module substructor (
  input  borrow_in,
  input  minuend,
  input  subtrahend,
  output difference,
  output borrow_out
);

  wire and_1_out, and_2_out, not_1_out, not_2_out, xor_1_out;

  not not_1 (not_1_out, minuend);
  xor xor_1 (xor_1_out, minuend, subtrahend);
  and and_1 (and_1_out, subtrahend, not_1_out);
  not not_2 (not_2_out, xor_1_out);
  and and_2 (and_2_out, not_2_out, borrow_in);
  xor xor_2 (difference, borrow_in, xor_1_out);
  or or_1 (borrow_out, and_2_out, and_1_out);
endmodule

module substructor_16bit (
  input  [15:0] subtrahend,
  input  [15:0] minuend,
  output [15:0] difference
);

  wire substructor_1_borrow_out, substructor_2_borrow_out, substructor_3_borrow_out,
       substructor_4_borrow_out, substructor_5_borrow_out, substructor_6_borrow_out,
       substructor_7_borrow_out, substructor_8_borrow_out, substructor_9_borrow_out,
       substructor_10_borrow_out, substructor_11_borrow_out, substructor_12_borrow_out,
       substructor_13_borrow_out, substructor_14_borrow_out, substructor_15_borrow_out,
       substructor_16_borrow_out;

  substructor substructor_1 (
    .borrow_in(1'b0), .minuend(minuend[0]), .subtrahend(subtrahend[0]), .difference(difference[0]),
    .borrow_out(substructor_1_borrow_out));
  substructor substructor_2 (
    .borrow_in(substructor_1_borrow_out), .minuend(minuend[1]), .subtrahend(subtrahend[1]),
    .difference(difference[1]), .borrow_out(substructor_2_borrow_out));
  substructor substructor_3 (
    .borrow_in(substructor_2_borrow_out), .minuend(minuend[2]), .subtrahend(subtrahend[2]),
    .difference(difference[2]), .borrow_out(substructor_3_borrow_out));
  substructor substructor_4 (
    .borrow_in(substructor_3_borrow_out), .minuend(minuend[3]), .subtrahend(subtrahend[3]),
    .difference(difference[3]), .borrow_out(substructor_4_borrow_out));
  substructor substructor_5 (
    .borrow_in(substructor_4_borrow_out), .minuend(minuend[4]), .subtrahend(subtrahend[4]),
    .difference(difference[4]), .borrow_out(substructor_5_borrow_out));
  substructor substructor_6 (
    .borrow_in(substructor_5_borrow_out), .minuend(minuend[5]), .subtrahend(subtrahend[5]),
    .difference(difference[5]), .borrow_out(substructor_6_borrow_out));
  substructor substructor_7 (
    .borrow_in(substructor_6_borrow_out), .minuend(minuend[6]), .subtrahend(subtrahend[6]),
    .difference(difference[6]), .borrow_out(substructor_7_borrow_out));
  substructor substructor_8 (
    .borrow_in(substructor_7_borrow_out), .minuend(minuend[7]), .subtrahend(subtrahend[7]),
    .difference(difference[7]), .borrow_out(substructor_8_borrow_out));
  substructor substructor_9 (
    .borrow_in(substructor_8_borrow_out), .minuend(minuend[8]), .subtrahend(subtrahend[8]),
    .difference(difference[8]), .borrow_out(substructor_9_borrow_out));
  substructor substructor_10 (
    .borrow_in(substructor_9_borrow_out), .minuend(minuend[9]), .subtrahend(subtrahend[9]),
    .difference(difference[9]), .borrow_out(substructor_10_borrow_out));
  substructor substructor_11 (
    .borrow_in(substructor_10_borrow_out), .minuend(minuend[10]), .subtrahend(subtrahend[10]),
    .difference(difference[10]), .borrow_out(substructor_11_borrow_out));
  substructor substructor_12 (
    .borrow_in(substructor_11_borrow_out), .minuend(minuend[11]), .subtrahend(subtrahend[11]),
    .difference(difference[11]), .borrow_out(substructor_12_borrow_out));
  substructor substructor_13 (
    .borrow_in(substructor_12_borrow_out), .minuend(minuend[12]), .subtrahend(subtrahend[12]),
    .difference(difference[12]), .borrow_out(substructor_13_borrow_out));
  substructor substructor_14 (
    .borrow_in(substructor_13_borrow_out), .minuend(minuend[13]), .subtrahend(subtrahend[13]),
    .difference(difference[13]), .borrow_out(substructor_14_borrow_out));
  substructor substructor_15 (
    .borrow_in(substructor_14_borrow_out), .minuend(minuend[14]), .subtrahend(subtrahend[14]),
    .difference(difference[14]), .borrow_out(substructor_15_borrow_out));
  substructor substructor_16 (
    .borrow_in(substructor_15_borrow_out), .minuend(minuend[15]), .subtrahend(subtrahend[15]),
    .difference(difference[15]), .borrow_out(substructor_16_borrow_out));
endmodule

module comparator_1bit (
  input  A,
  input  B,
  input  oldA_smaller_oldB,
  input  oldA_equal_oldB,
  input  oldA_bigger_oldB,
  output A_smaller_B,
  output A_equal_B,
  output A_bigger_B
);

  wire and_1_out, and_2_out, and_3_out, and_5_out, not_1_out, xor_1_out;

  and and_1 (and_1_out, ~A, B);  // AND_Gate
  xor xor_1 (xor_1_out, A, B);
  and and_2 (and_2_out, A, ~B);  // AND_Gate
  not not_1 (not_1_out, xor_1_out);
  and and_3 (and_3_out, oldA_smaller_oldB, not_1_out);
  and and_4 (A_equal_B, not_1_out, oldA_equal_oldB);
  and and_5 (and_5_out, oldA_bigger_oldB, not_1_out);
  or or_1 (A_smaller_B, and_1_out, and_3_out);
  or or_2 (A_bigger_B, and_5_out, and_2_out);
endmodule

module summator_1bit (
  input  A,
  input  B,
  input  borrow_in,
  output Sum,
  output Borrow_out
);

  wire and_1_out, and_2_out, xor_1_out;

  and and_1 (and_1_out, A, B);
  xor xor_1 (xor_1_out, A, B);
  xor xor_2 (Sum, xor_1_out, borrow_in);
  and and_2 (and_2_out, xor_1_out, borrow_in);
  or or_1 (Borrow_out, and_2_out, and_1_out);
endmodule

module summator_4bit (
  input  [3:0] A,
  input  [3:0] B,
  input  Borrow_in,
  output [3:0] IO_OUT,
  output Borrow_out
);

  wire summator_1bit_1_borrow_out, summator_1bit_2_borrow_out, summator_1bit_3_borrow_out;

  summator_1bit summator_1bit_1 (
    .A(A[0]), .B(B[0]), .borrow_in(Borrow_in), .Sum(IO_OUT[0]), .Borrow_out(summator_1bit_1_borrow_out));
  summator_1bit summator_1bit_2 (
    .A(A[1]), .B(B[1]), .borrow_in(summator_1bit_1_borrow_out), .Sum(IO_OUT[1]),
    .Borrow_out(summator_1bit_2_borrow_out));
  summator_1bit summator_1bit_3 (
    .A(A[2]), .B(B[2]), .borrow_in(summator_1bit_2_borrow_out), .Sum(IO_OUT[2]),
    .Borrow_out(summator_1bit_3_borrow_out));
  summator_1bit summator_1bit_4 (
    .A(A[3]), .B(B[3]), .borrow_in(summator_1bit_3_borrow_out), .Sum(IO_OUT[3]), .Borrow_out(Borrow_out));
endmodule

module synch_rs_trigger (
  input  R,
  input  C,
  input  S,
  input  ENABLE,
  output Q,
  output NQ
);

  wire and_1_out, and_2_out, nor_2_out, or_1_out, por_1_out;

  POR por_1 (.out(por_1_out));
  and and_1 (and_1_out, R, C);
  and and_2 (and_2_out, C, S);
  or or_1 (or_1_out, ENABLE, por_1_out);
  nor nor_1 (Q, and_1_out, NQ);
  nor nor_2 (nor_2_out, Q, and_2_out);
  or or_2 (NQ, nor_2_out, or_1_out);
endmodule

module d_trigger (
  input  C,
  input  D,
  input  ENABLE,
  output Q,
  output NQ
);

  wire not_1_out;

  not not_1 (not_1_out, D);
  synch_rs_trigger synch_rs_trigger_1 (.R(not_1_out), .C(C), .S(D), .ENABLE(ENABLE), .Q(Q), .NQ(NQ));
endmodule

module comparator_16bit (
  input  [15:0] B,
  input  [15:0] A,
  output A_smaller_B,
  output A_equal_B,
  output A_bigger_B
);

  wire comparator_1bit_2_a_bigger_b, comparator_1bit_2_a_equal_b, comparator_1bit_2_a_smaller_b,
       comparator_1bit_3_a_bigger_b, comparator_1bit_3_a_equal_b, comparator_1bit_3_a_smaller_b,
       comparator_1bit_4_a_bigger_b, comparator_1bit_4_a_equal_b, comparator_1bit_4_a_smaller_b,
       comparator_1bit_5_a_bigger_b, comparator_1bit_5_a_equal_b, comparator_1bit_5_a_smaller_b,
       comparator_1bit_6_a_bigger_b, comparator_1bit_6_a_equal_b, comparator_1bit_6_a_smaller_b,
       comparator_1bit_7_a_bigger_b, comparator_1bit_7_a_equal_b, comparator_1bit_7_a_smaller_b,
       comparator_1bit_8_a_bigger_b, comparator_1bit_8_a_equal_b, comparator_1bit_8_a_smaller_b,
       comparator_1bit_9_a_bigger_b, comparator_1bit_9_a_equal_b, comparator_1bit_9_a_smaller_b,
       comparator_1bit_10_a_bigger_b, comparator_1bit_10_a_equal_b, comparator_1bit_10_a_smaller_b,
       comparator_1bit_11_a_bigger_b, comparator_1bit_11_a_equal_b, comparator_1bit_11_a_smaller_b,
       comparator_1bit_12_a_bigger_b, comparator_1bit_12_a_equal_b, comparator_1bit_12_a_smaller_b,
       comparator_1bit_13_a_bigger_b, comparator_1bit_13_a_equal_b, comparator_1bit_13_a_smaller_b,
       comparator_1bit_14_a_bigger_b, comparator_1bit_14_a_equal_b, comparator_1bit_14_a_smaller_b,
       comparator_1bit_15_a_bigger_b, comparator_1bit_15_a_equal_b, comparator_1bit_15_a_smaller_b,
       comparator_1bit_16_a_bigger_b, comparator_1bit_16_a_equal_b, comparator_1bit_16_a_smaller_b;

  comparator_1bit comparator_1bit_1 (
    .A(A[15]), .B(B[15]), .oldA_smaller_oldB(comparator_1bit_2_a_smaller_b),
    .oldA_equal_oldB(comparator_1bit_2_a_equal_b), .oldA_bigger_oldB(comparator_1bit_2_a_bigger_b),
    .A_smaller_B(A_smaller_B), .A_equal_B(A_equal_B), .A_bigger_B(A_bigger_B));
  comparator_1bit comparator_1bit_2 (
    .A(A[14]), .B(B[14]), .oldA_smaller_oldB(comparator_1bit_3_a_smaller_b),
    .oldA_equal_oldB(comparator_1bit_3_a_equal_b), .oldA_bigger_oldB(comparator_1bit_3_a_bigger_b),
    .A_smaller_B(comparator_1bit_2_a_smaller_b), .A_equal_B(comparator_1bit_2_a_equal_b),
    .A_bigger_B(comparator_1bit_2_a_bigger_b));
  comparator_1bit comparator_1bit_3 (
    .A(A[13]), .B(B[13]), .oldA_smaller_oldB(comparator_1bit_4_a_smaller_b),
    .oldA_equal_oldB(comparator_1bit_4_a_equal_b), .oldA_bigger_oldB(comparator_1bit_4_a_bigger_b),
    .A_smaller_B(comparator_1bit_3_a_smaller_b), .A_equal_B(comparator_1bit_3_a_equal_b),
    .A_bigger_B(comparator_1bit_3_a_bigger_b));
  comparator_1bit comparator_1bit_4 (
    .A(A[12]), .B(B[12]), .oldA_smaller_oldB(comparator_1bit_5_a_smaller_b),
    .oldA_equal_oldB(comparator_1bit_5_a_equal_b), .oldA_bigger_oldB(comparator_1bit_5_a_bigger_b),
    .A_smaller_B(comparator_1bit_4_a_smaller_b), .A_equal_B(comparator_1bit_4_a_equal_b),
    .A_bigger_B(comparator_1bit_4_a_bigger_b));
  comparator_1bit comparator_1bit_5 (
    .A(A[11]), .B(B[11]), .oldA_smaller_oldB(comparator_1bit_6_a_smaller_b),
    .oldA_equal_oldB(comparator_1bit_6_a_equal_b), .oldA_bigger_oldB(comparator_1bit_6_a_bigger_b),
    .A_smaller_B(comparator_1bit_5_a_smaller_b), .A_equal_B(comparator_1bit_5_a_equal_b),
    .A_bigger_B(comparator_1bit_5_a_bigger_b));
  comparator_1bit comparator_1bit_6 (
    .A(A[10]), .B(B[10]), .oldA_smaller_oldB(comparator_1bit_7_a_smaller_b),
    .oldA_equal_oldB(comparator_1bit_7_a_equal_b), .oldA_bigger_oldB(comparator_1bit_7_a_bigger_b),
    .A_smaller_B(comparator_1bit_6_a_smaller_b), .A_equal_B(comparator_1bit_6_a_equal_b),
    .A_bigger_B(comparator_1bit_6_a_bigger_b));
  comparator_1bit comparator_1bit_7 (
    .A(A[9]), .B(B[9]), .oldA_smaller_oldB(comparator_1bit_8_a_smaller_b),
    .oldA_equal_oldB(comparator_1bit_8_a_equal_b), .oldA_bigger_oldB(comparator_1bit_8_a_bigger_b),
    .A_smaller_B(comparator_1bit_7_a_smaller_b), .A_equal_B(comparator_1bit_7_a_equal_b),
    .A_bigger_B(comparator_1bit_7_a_bigger_b));
  comparator_1bit comparator_1bit_8 (
    .A(A[8]), .B(B[8]), .oldA_smaller_oldB(comparator_1bit_9_a_smaller_b),
    .oldA_equal_oldB(comparator_1bit_9_a_equal_b), .oldA_bigger_oldB(comparator_1bit_9_a_bigger_b),
    .A_smaller_B(comparator_1bit_8_a_smaller_b), .A_equal_B(comparator_1bit_8_a_equal_b),
    .A_bigger_B(comparator_1bit_8_a_bigger_b));
  comparator_1bit comparator_1bit_9 (
    .A(A[7]), .B(B[7]), .oldA_smaller_oldB(comparator_1bit_10_a_smaller_b),
    .oldA_equal_oldB(comparator_1bit_10_a_equal_b), .oldA_bigger_oldB(comparator_1bit_10_a_bigger_b),
    .A_smaller_B(comparator_1bit_9_a_smaller_b), .A_equal_B(comparator_1bit_9_a_equal_b),
    .A_bigger_B(comparator_1bit_9_a_bigger_b));
  comparator_1bit comparator_1bit_10 (
    .A(A[6]), .B(B[6]), .oldA_smaller_oldB(comparator_1bit_11_a_smaller_b),
    .oldA_equal_oldB(comparator_1bit_11_a_equal_b), .oldA_bigger_oldB(comparator_1bit_11_a_bigger_b),
    .A_smaller_B(comparator_1bit_10_a_smaller_b), .A_equal_B(comparator_1bit_10_a_equal_b),
    .A_bigger_B(comparator_1bit_10_a_bigger_b));
  comparator_1bit comparator_1bit_11 (
    .A(A[5]), .B(B[5]), .oldA_smaller_oldB(comparator_1bit_12_a_smaller_b),
    .oldA_equal_oldB(comparator_1bit_12_a_equal_b), .oldA_bigger_oldB(comparator_1bit_12_a_bigger_b),
    .A_smaller_B(comparator_1bit_11_a_smaller_b), .A_equal_B(comparator_1bit_11_a_equal_b),
    .A_bigger_B(comparator_1bit_11_a_bigger_b));
  comparator_1bit comparator_1bit_12 (
    .A(A[4]), .B(B[4]), .oldA_smaller_oldB(comparator_1bit_13_a_smaller_b),
    .oldA_equal_oldB(comparator_1bit_13_a_equal_b), .oldA_bigger_oldB(comparator_1bit_13_a_bigger_b),
    .A_smaller_B(comparator_1bit_12_a_smaller_b), .A_equal_B(comparator_1bit_12_a_equal_b),
    .A_bigger_B(comparator_1bit_12_a_bigger_b));
  comparator_1bit comparator_1bit_13 (
    .A(A[3]), .B(B[3]), .oldA_smaller_oldB(comparator_1bit_14_a_smaller_b),
    .oldA_equal_oldB(comparator_1bit_14_a_equal_b), .oldA_bigger_oldB(comparator_1bit_14_a_bigger_b),
    .A_smaller_B(comparator_1bit_13_a_smaller_b), .A_equal_B(comparator_1bit_13_a_equal_b),
    .A_bigger_B(comparator_1bit_13_a_bigger_b));
  comparator_1bit comparator_1bit_14 (
    .A(A[2]), .B(B[2]), .oldA_smaller_oldB(comparator_1bit_15_a_smaller_b),
    .oldA_equal_oldB(comparator_1bit_15_a_equal_b), .oldA_bigger_oldB(comparator_1bit_15_a_bigger_b),
    .A_smaller_B(comparator_1bit_14_a_smaller_b), .A_equal_B(comparator_1bit_14_a_equal_b),
    .A_bigger_B(comparator_1bit_14_a_bigger_b));
  comparator_1bit comparator_1bit_15 (
    .A(A[1]), .B(B[1]), .oldA_smaller_oldB(comparator_1bit_16_a_smaller_b),
    .oldA_equal_oldB(comparator_1bit_16_a_equal_b), .oldA_bigger_oldB(comparator_1bit_16_a_bigger_b),
    .A_smaller_B(comparator_1bit_15_a_smaller_b), .A_equal_B(comparator_1bit_15_a_equal_b),
    .A_bigger_B(comparator_1bit_15_a_bigger_b));
  comparator_1bit comparator_1bit_16 (
    .A(A[0]), .B(B[0]), .oldA_smaller_oldB(1'b0), .oldA_equal_oldB(1'b1), .oldA_bigger_oldB(1'b0),
    .A_smaller_B(comparator_1bit_16_a_smaller_b), .A_equal_B(comparator_1bit_16_a_equal_b),
    .A_bigger_B(comparator_1bit_16_a_bigger_b));
endmodule

module memory_cell_16bit (
  input  [15:0] IO_DATA_IN,
  input  C,
  input  ENABLE,
  output [15:0] out_4
);

  wire d_trigger_1_nq, d_trigger_2_nq, d_trigger_3_nq, d_trigger_4_nq, d_trigger_5_nq, d_trigger_6_nq,
       d_trigger_7_nq, d_trigger_8_nq, d_trigger_9_nq, d_trigger_10_nq, d_trigger_11_nq, d_trigger_12_nq,
       d_trigger_13_nq, d_trigger_14_nq, d_trigger_15_nq, d_trigger_16_nq, not_1_out;

  not not_1 (not_1_out, ENABLE);
  d_trigger d_trigger_1 (.C(C), .D(IO_DATA_IN[0]), .ENABLE(not_1_out), .Q(out_4[0]), .NQ(d_trigger_1_nq));
  // NoConnect on d_trigger_1_nq
  d_trigger d_trigger_2 (.C(C), .D(IO_DATA_IN[1]), .ENABLE(not_1_out), .Q(out_4[1]), .NQ(d_trigger_2_nq));
  // NoConnect on d_trigger_2_nq
  d_trigger d_trigger_3 (.C(C), .D(IO_DATA_IN[2]), .ENABLE(not_1_out), .Q(out_4[2]), .NQ(d_trigger_3_nq));
  // NoConnect on d_trigger_3_nq
  d_trigger d_trigger_4 (.C(C), .D(IO_DATA_IN[3]), .ENABLE(not_1_out), .Q(out_4[3]), .NQ(d_trigger_4_nq));
  // NoConnect on d_trigger_4_nq
  d_trigger d_trigger_5 (.C(C), .D(IO_DATA_IN[4]), .ENABLE(not_1_out), .Q(out_4[4]), .NQ(d_trigger_5_nq));
  // NoConnect on d_trigger_5_nq
  d_trigger d_trigger_6 (.C(C), .D(IO_DATA_IN[5]), .ENABLE(not_1_out), .Q(out_4[5]), .NQ(d_trigger_6_nq));
  // NoConnect on d_trigger_6_nq
  d_trigger d_trigger_7 (.C(C), .D(IO_DATA_IN[6]), .ENABLE(not_1_out), .Q(out_4[6]), .NQ(d_trigger_7_nq));
  // NoConnect on d_trigger_7_nq
  d_trigger d_trigger_8 (.C(C), .D(IO_DATA_IN[7]), .ENABLE(not_1_out), .Q(out_4[7]), .NQ(d_trigger_8_nq));
  // NoConnect on d_trigger_8_nq
  d_trigger d_trigger_9 (.C(C), .D(IO_DATA_IN[8]), .ENABLE(not_1_out), .Q(out_4[8]), .NQ(d_trigger_9_nq));
  // NoConnect on d_trigger_9_nq
  d_trigger d_trigger_10 (.C(C), .D(IO_DATA_IN[9]), .ENABLE(not_1_out), .Q(out_4[9]), .NQ(d_trigger_10_nq));
  // NoConnect on d_trigger_10_nq
  d_trigger d_trigger_11 (.C(C), .D(IO_DATA_IN[10]), .ENABLE(not_1_out), .Q(out_4[10]), .NQ(d_trigger_11_nq));
  // NoConnect on d_trigger_11_nq
  d_trigger d_trigger_12 (.C(C), .D(IO_DATA_IN[11]), .ENABLE(not_1_out), .Q(out_4[11]), .NQ(d_trigger_12_nq));
  // NoConnect on d_trigger_12_nq
  d_trigger d_trigger_13 (.C(C), .D(IO_DATA_IN[12]), .ENABLE(not_1_out), .Q(out_4[12]), .NQ(d_trigger_13_nq));
  // NoConnect on d_trigger_13_nq
  d_trigger d_trigger_14 (.C(C), .D(IO_DATA_IN[13]), .ENABLE(not_1_out), .Q(out_4[13]), .NQ(d_trigger_14_nq));
  // NoConnect on d_trigger_14_nq
  d_trigger d_trigger_15 (.C(C), .D(IO_DATA_IN[14]), .ENABLE(not_1_out), .Q(out_4[14]), .NQ(d_trigger_15_nq));
  // NoConnect on d_trigger_15_nq
  d_trigger d_trigger_16 (.C(C), .D(IO_DATA_IN[15]), .ENABLE(not_1_out), .Q(out_4[15]), .NQ(d_trigger_16_nq));
  // NoConnect on d_trigger_16_nq
endmodule

module summator_16bit (
  input  [15:0] A,
  input  Borrow_in,
  input  [15:0] B,
  output [15:0] IO_OUT,
  output Borrow_out
);

  wire summator_4bit_1_borrow_out, summator_4bit_2_borrow_out, summator_4bit_3_borrow_out;

  summator_4bit summator_4bit_1 (
    .A(A[3:0]), .B(B[3:0]), .Borrow_in(Borrow_in), .IO_OUT(IO_OUT[3:0]),
    .Borrow_out(summator_4bit_1_borrow_out));
  summator_4bit summator_4bit_2 (
    .A(A[7:4]), .B(B[7:4]), .Borrow_in(summator_4bit_1_borrow_out), .IO_OUT(IO_OUT[7:4]),
    .Borrow_out(summator_4bit_2_borrow_out));
  summator_4bit summator_4bit_3 (
    .A(A[11:8]), .B(B[11:8]), .Borrow_in(summator_4bit_2_borrow_out), .IO_OUT(IO_OUT[11:8]),
    .Borrow_out(summator_4bit_3_borrow_out));
  summator_4bit summator_4bit_4 (
    .A(A[15:12]), .B(B[15:12]), .Borrow_in(summator_4bit_3_borrow_out), .IO_OUT(IO_OUT[15:12]),
    .Borrow_out(Borrow_out));
endmodule

module if_expression (
  input  [15:0] A,
  input  expression,
  input  [15:0] B,
  output [15:0] IO_OUT
);

  wire not_1_out;

  not not_1 (not_1_out, expression);
  Transistor #(.\type ("n"), .width(16)) transistor_1 (.in(A), .out(IO_OUT), .gate(expression));
  Transistor #(.\type ("n"), .width(16)) transistor_2 (.in(B), .out(IO_OUT), .gate(not_1_out));
  Pull_Resistor #(.pull(1)) pull_resistor_1 (.node(IO_OUT));
endmodule

module get_info (
  input  [15:0] IO_IN,
  output [9:0] mantissa,
  output [4:0] exp,
  output sign
);


  assign exp = IO_IN[14:10];
  assign mantissa = IO_IN[9:0];
  assign sign = IO_IN[15];
endmodule

module is_nan (
  input  [9:0] mant,
  input  [4:0] exp,
  output NAN
);

  wire and_1_out, or_1_out;

  and and_1 (and_1_out, exp[0], exp[1], exp[2], exp[3], exp[4]);
  or or_1 (or_1_out, mant[0], mant[1], mant[2], mant[3], mant[4], mant[5], mant[6], mant[7], mant[8], mant[9]);
  and and_2 (NAN, or_1_out, and_1_out);
endmodule

module is_pinf (
  input  [9:0] mant,
  input  [4:0] exp,
  input  sign,
  output PINF
);

  wire and_1_out, or_1_out;

  and and_1 (and_1_out, exp[0], exp[1], exp[2], exp[3], exp[4]);
  or or_1 (or_1_out, mant[0], mant[1], mant[2], mant[3], mant[4], mant[5], mant[6], mant[7], mant[8], mant[9]);
  and and_2 (PINF, ~or_1_out, ~sign, and_1_out);  // AND_Gate
endmodule

module is_ninf (
  input  [9:0] mant,
  input  [4:0] exp,
  input  sign,
  output PINF
);

  wire and_1_out, or_1_out;

  and and_1 (and_1_out, exp[0], exp[1], exp[2], exp[3], exp[4]);
  or or_1 (or_1_out, mant[0], mant[1], mant[2], mant[3], mant[4], mant[5], mant[6], mant[7], mant[8], mant[9]);
  and and_2 (PINF, ~or_1_out, sign, and_1_out);  // AND_Gate
endmodule

module special_cases (
  input  [9:0] mant,
  input  [4:0] exp,
  input  sign,
  output NAN,
  output PINF,
  output NINF
);

  is_nan is_nan_1 (.mant(mant), .exp(exp), .NAN(NAN));
  is_pinf is_pinf_1 (.mant(mant), .exp(exp), .sign(sign), .PINF(PINF));
  is_ninf is_ninf_1 (.mant(mant), .exp(exp), .sign(sign), .PINF(NINF));
endmodule

module correct_exp (
  input  [4:0] DATA_IN,
  output [4:0] DATA_OUT
);

  wire or_1_out, summator_16bit_1_borrow_out, undriven, xor_1_out;
  wire [0:0] summator_16bit_1_io_out;
  wire [14:0] summator_16bit_1_io_out_2;
  wire [15:0] if_expression_2_io_out, shift_right_1_io_out, substructor_16bit_1_difference;
  wire [15:5] if_expression_1_io_out;

  or or_1 (or_1_out, DATA_IN[0], DATA_IN[1], DATA_IN[2], DATA_IN[3], DATA_IN[4]);
  // NoConnect on undriven
  summator_16bit summator_16bit_1 (
    .A(16'hf), .Borrow_in(undriven), .B({{11{1'b0}}, DATA_IN}),
    .IO_OUT({summator_16bit_1_io_out_2, summator_16bit_1_io_out[0]}), .Borrow_out(summator_16bit_1_borrow_out));
  // NoConnect on summator_16bit_1_borrow_out
  xor xor_1 (xor_1_out, summator_16bit_1_io_out[0], 1'b0);
  substructor_16bit substructor_16bit_1 (
    .subtrahend(16'h1), .minuend({summator_16bit_1_io_out_2, summator_16bit_1_io_out[0]}),
    .difference(substructor_16bit_1_difference));
  if_expression if_expression_1 (
    .A(shift_right_1_io_out), .expression(or_1_out), .B({16{1'b0}}),
    .IO_OUT({if_expression_1_io_out, DATA_OUT}));
  if_expression if_expression_2 (
    .A(substructor_16bit_1_difference), .expression(xor_1_out),
    .B({summator_16bit_1_io_out_2, summator_16bit_1_io_out[0]}), .IO_OUT(if_expression_2_io_out));
  shift_right shift_right_1 (.IO_IN(if_expression_2_io_out), .IO_OUT(shift_right_1_io_out));
endmodule

module correct_mant (
  input  [4:0] exp,
  input  [10:0] mantissa,
  output [10:0] full_mantissa
);

  wire or_1_out, summator_16bit_1_borrow_out, undriven;
  wire [15:0] bit_extender_1_out, if_expression_1_io_out, summator_16bit_1_io_out;

  assign bit_extender_1_out = {{5{1'b0}}, mantissa};  // Bit_Extender bit_extender_1
  // NoConnect on undriven
  or or_1 (or_1_out, exp[0], exp[1], exp[2], exp[3], exp[4]);
  summator_16bit summator_16bit_1 (
    .A(16'h400), .Borrow_in(undriven), .B(bit_extender_1_out), .IO_OUT(summator_16bit_1_io_out),
    .Borrow_out(summator_16bit_1_borrow_out));
  // NoConnect on summator_16bit_1_borrow_out
  if_expression if_expression_1 (
    .A(summator_16bit_1_io_out), .expression(or_1_out), .B(bit_extender_1_out),
    .IO_OUT(if_expression_1_io_out));
  Bit_Extender #(.in_width(16), .out_width(11), .\type ("zero")) bit_extender_2 (
    .in(if_expression_1_io_out), .out(full_mantissa));
endmodule

module shift_right (
  input  [15:0] IO_IN,
  output [15:0] IO_OUT
);

  // NoConnect on IO_IN[0]

  assign IO_OUT = {1'b0, IO_IN[15:1]};
endmodule
